// Logisim project SingleCycle.circ as structural Verilog: 2 circuits, main circuit main
module main (
  output [3:0] out_1,
  output [1:0] out_2,
  output [3:0] out_3
);

  wire ALUSrc, and_1_out, Branch, Clk, Jump, MemRead, MemtoReg, MemWrite, mips_alu_1_p4, RegDest,
       registerfile_1_p5, RegWrite;
  wire [3:0] adder_1_p3;
  wire [4:0] multiplexer_1_out;
  wire [23:0] bit_extender_3_out;
  wire [27:0] adder_1_p3_2, bit_extender_1_out, shifter_1_out;
  wire [31:0] adder_2_p3, bit_extender_2_out, mips_alu_1_p5, mips_ram_1_p6, mipsprogramrom_1_p1,
       multiplexer_2_out, multiplexer_3_out, multiplexer_4_out, PC_q, registerfile_1_p4, registerfile_1_p6,
       shifter_2_out;

  Clock clock_1 (.out(Clk));
  Register #(.width(32)) PC (.D(multiplexer_4_out), .Q(PC_q), .clk(Clk));  // open: en, clr
  // PLA Control: pin names not known; wires that end beside it: registerfile_1_p4[31:26], PC_q, {RegWrite, ALUSrc, MemWrite, out_2, MemtoReg, MemRead, Branch, Jump, RegDest}
  // Adder adder_1: pin names not known; wires that end beside it: PC_q, 32'h4, {adder_1_p3, adder_1_p3_2}
  // MIPSProgramROM mipsprogramrom_1: pin names not known; wires that end beside it: mipsprogramrom_1_p1, Clk
  assign bit_extender_1_out = {{2{1'b0}}, registerfile_1_p4[25:0]};  // Bit_Extender bit_extender_1
  Shifter #(.width(28)) shifter_1 (.in(bit_extender_1_out), .\dist (5'b00010), .out(shifter_1_out));
  Multiplexer #(.width(5), .enable("false")) multiplexer_1 (
    .in0(registerfile_1_p4[20:16]), .in1(registerfile_1_p4[15:11]), .out(multiplexer_1_out), .sel(RegDest));
  // RegisterFile registerfile_1: pin names not known; wires that end beside it: RegWrite, multiplexer_1_out, registerfile_1_p4[25:21], registerfile_1_p4[20:16], registerfile_1_p5, registerfile_1_p6
  assign bit_extender_2_out = {{16{1'b0}}, registerfile_1_p4[15:0]};  // Bit_Extender bit_extender_2
  Shifter #(.width(32)) shifter_2 (.in(bit_extender_2_out), .\dist (5'b00010), .out(shifter_2_out));
  Multiplexer #(.width(32), .enable("false")) multiplexer_2 (
    .in0(registerfile_1_p6), .in1(bit_extender_2_out), .out(multiplexer_2_out), .sel(ALUSrc));
  ALU_control alu_control_1 (.in_1({out_2, registerfile_1_p4[5:0]}), .out_2(out_1));
  // MIPS_ALU mips_alu_1: pin names not known; wires that end beside it: registerfile_1_p5, multiplexer_2_out, out_1, mips_alu_1_p4, mips_alu_1_p5
  // Adder adder_2: pin names not known; wires that end beside it: {adder_1_p3, adder_1_p3_2}, shifter_2_out, adder_2_p3
  Bit_Extender #(.in_width(32), .out_width(24)) bit_extender_3 (.in(mips_alu_1_p5), .out(bit_extender_3_out));
  Multiplexer #(.width(32), .enable("false")) multiplexer_3 (
    .in0({adder_1_p3, adder_1_p3_2}), .in1(adder_2_p3), .out(multiplexer_3_out), .sel(and_1_out));
  and and_1 (and_1_out, Branch, mips_alu_1_p4);
  Multiplexer #(.width(32), .enable("false")) multiplexer_4 (
    .in0(multiplexer_3_out), .in1({adder_1_p3, shifter_1_out}), .out(multiplexer_4_out), .sel(Jump));
  Multiplexer #(.width(32), .enable("false")) multiplexer_5 (
    .in0(mips_alu_1_p5), .in1(mips_ram_1_p6), .out(mipsprogramrom_1_p1), .sel(MemtoReg));
  // MIPS_RAM mips_ram_1: pin names not known; wires that end beside it: bit_extender_3_out, registerfile_1_p6, MemWrite, MemRead, Clk, mips_ram_1_p6

  // Other names for the same wires on the sheet: ALUop[1:0] = out_2
endmodule

module ALU_control (
  input  [7:0] in_1,
  output [3:0] out_2
);

  // PLA ALU_ctrl: pin names not known; wires that end beside it: in_1, out_2
endmodule
