// Logisim project sandbox.circ as structural Verilog: 7 circuits, main circuit main
module main (
  output [31:0] Jump_Address,
  output [31:0] Fetched_Instruction,
  output [31:0] A,
  output [31:0] A_2,
  output [31:0] B,
  output [31:0] B_2,
  output [31:0] Result,
  output [31:0] Next_Instruction,
  output [31:0] Data,
  output [5:0] Operation_Code,
  output [4:0] Operation_Code_2,
  output [31:0] B_3,
  output [31:0] Result_2,
  output [31:0] _0_15,
  output [31:0] _0_15_2,
  output [3:0] out_16,
  output [31:0] Write_Back,
  output [1:0] out_18,
  output [2:0] out_19
);

  wire ALUSrc, Branch, comparator_1_eq, comparator_2_eq, comparator_3_eq, ex_mem_1_memread__out,
       ex_mem_1_memtoreg__out, ex_mem_1_memwrite__out, ex_mem_1_regwrite__out, id_ex_1_p17, id_ex_1_p18,
       id_ex_1_p19, id_ex_1_p20, id_ex_1_p21, id_ex_1_p23, Jump, JumpReg, mem_wb_1_memtoreg__out, MemRead,
       MemToReg, MemWrite, nor_1_out, not_1_out, not_3_out, not_4_out, RegDst, registerfile_1_p3, RegWrite,
       Tick, undriven;
  wire [1:0] ALUOp;
  wire [3:0] alu_control_1_out_2, mips_alu_1_p3;
  wire [4:0] ex_mem_1_regdest__out, id_ex_1_p27, id_ex_1_p28, multiplexer_6_out, multiplexer_7_out,
       registerfile_1_p4;
  wire [5:3] id_ex_1_p29;
  wire [23:0] bit_extender_3_out;
  wire [27:0] bit_extender_1_out, if_id_1_pc__out;
  wire [31:0] adder_1_p4, adder_2_p4, adder_3_p2, adder_3_p3, ex_mem_1_inst___out, id_ex_1_p24,
       mem_wb_1_address__out, mem_wb_1_read_data__out, mips_alu_1_p2, multiplexer_1_out, multiplexer_2_out,
       multiplexer_3_out, multiplexer_4_out, multiplexer_5_out, multiplexer_10_out, multiplexer_11_out, PC_q;

  Multiplexer #(.width(32), .enable("false")) multiplexer_1 (
    .in0(multiplexer_3_out), .in1(adder_1_p4), .out(multiplexer_1_out), .sel(nor_1_out));
  nor nor_1 (nor_1_out, Jump, Branch);
  Register #(.width(32)) PC (.D(multiplexer_1_out), .Q(PC_q), .clk(Tick));  // open: en, clr
  // Adder adder_1: pin names not known; wires that end beside it: PC_q, 32'h4, JumpReg, adder_1_p4
  // Adder adder_2: pin names not known; wires that end beside it: PC_q, 32'h8, PC_q, adder_2_p4
  Clock clock_1 (.out(Tick));
  // MIPSProgramROM mipsprogramrom_1: pin names not known; wires that end beside it: Next_Instruction
  IF_ID if_id_1 (
    .Clock(Tick), .PC__in(adder_1_p4), .Inst___in(Next_Instruction),
    .PC__out({Jump_Address[31:28], if_id_1_pc__out}), .Inst___out(Fetched_Instruction));
  // PLA Control: pin names not known; wires that end beside it: Fetched_Instruction[31:26]
  assign bit_extender_1_out = {{2{1'b0}}, Fetched_Instruction[25:0]};  // Bit_Extender bit_extender_1
  Multiplexer #(.width(32), .enable("false")) multiplexer_2 (
    .in0(adder_2_p4), .in1(Write_Back), .out(multiplexer_2_out), .sel(not_1_out));
  not not_1 (not_1_out, Jump);
  Shifter #(.width(28)) shifter_1 (.in(bit_extender_1_out), .\dist (5'b00010), .out(Jump_Address[27:0]));
  // RegisterFile registerfile_1: pin names not known; wires that end beside it: multiplexer_2_out, Tick, registerfile_1_p3, registerfile_1_p4, Fetched_Instruction[25:21], Fetched_Instruction[20:16], A, B
  assign _0_15 = {{16{Fetched_Instruction[15]}}, Fetched_Instruction[15:0]};  // Bit_Extender bit_extender_2
  Comparator #(.width(6)) comparator_1 (.a(6'b001000), .b(_0_15[5:0]), .eq(comparator_1_eq));  // open: gt, lt
  not not_2 (JumpReg, comparator_1_eq);
  Multiplexer #(.width(32), .enable("false")) multiplexer_3 (
    .in0(A), .in1(multiplexer_4_out), .out(multiplexer_3_out), .sel(JumpReg));
  Multiplexer #(.width(32), .enable("false")) multiplexer_4 (
    .in0(multiplexer_5_out), .in1(Jump_Address), .out(multiplexer_4_out), .sel(Jump));
  Comparator #(.width(32), .mode("unsigned")) comparator_2 (.a(A), .b(B), .eq(comparator_2_eq));  // open: gt, lt
  // Adder adder_3: pin names not known; wires that end beside it: {Jump_Address[31:28], if_id_1_pc__out}, adder_3_p2, adder_3_p3
  Shifter #(.width(32)) shifter_2 (.in(_0_15), .\dist (5'b00010), .out(adder_3_p2));
  Multiplexer #(.width(32), .enable("false")) multiplexer_5 (
    .in0({Jump_Address[31:28], if_id_1_pc__out}), .in1(adder_3_p3), .out(multiplexer_5_out),
    .sel(comparator_2_eq));
  // ID_EX id_ex_1: pin names not known; wires that end beside it: RegDst, MemToReg, RegWrite, MemRead, MemWrite, ALUSrc, ALUOp, Jump, {Jump_Address[31:28], if_id_1_pc__out}, A, B, Fetched_Instruction[20:16], Fetched_Instruction[15:11], Fetched_Instruction[31:26], _0_15, Tick, id_ex_1_p17, id_ex_1_p18, id_ex_1_p19, id_ex_1_p20, id_ex_1_p21, out_18, id_ex_1_p23, id_ex_1_p24, A_2, B_2, id_ex_1_p27, id_ex_1_p28, {id_ex_1_p29, out_19}, _0_15_2
  Multiplexer #(.width(5), .enable("false")) multiplexer_6 (
    .in0(id_ex_1_p27), .in1(id_ex_1_p28), .out(multiplexer_6_out), .sel(undriven));
  Multiplexer #(.width(5), .enable("false")) multiplexer_7 (
    .in0(multiplexer_6_out), .in1({5{1'b1}}), .out(multiplexer_7_out), .sel(id_ex_1_p23));
  ALU_control alu_control_1 (.in_1({out_18, _0_15_2[5:0]}), .out_2(alu_control_1_out_2));
  // MIPS_ALU mips_alu_1: pin names not known; wires that end beside it: A_2, mips_alu_1_p2, mips_alu_1_p3, Result
  Multiplexer #(.width(32), .enable("false")) multiplexer_8 (
    .in0(B_2), .in1(_0_15_2), .out(mips_alu_1_p2), .sel(id_ex_1_p21));
  Multiplexer #(.width(4), .enable("false")) multiplexer_9 (
    .in0(alu_control_1_out_2), .in1(out_16), .out(mips_alu_1_p3), .sel(alu_control_1_out_2[3]));
  Imm__Ctrl imm_ctrl_1 (.in_1(out_19), .out_2(out_16));
  not not_3 (not_3_out, id_ex_1_p23);
  Multiplexer #(.width(32), .enable("false")) multiplexer_10 (
    .in0(Jump_Address), .in1(id_ex_1_p24), .out(multiplexer_10_out), .sel(not_3_out));
  Multiplexer #(.width(32), .enable("false")) multiplexer_11 (
    .in0(multiplexer_10_out), .in1(Result), .out(multiplexer_11_out), .sel(comparator_3_eq));
  Comparator #(.width(6)) comparator_3 (.a(6'b001000), .b(_0_15_2[5:0]), .eq(comparator_3_eq));  // open: gt, lt
  EX_MEM ex_mem_1 (
    .Clock(Tick), .Result__in(Result), .Inst___in(B_2), .Result__out(Result_2),
    .inst___out(ex_mem_1_inst___out), .MemToReg__in(id_ex_1_p17), .MemToReg__out(ex_mem_1_memtoreg__out),
    .MemRead__in(id_ex_1_p19), .MemRead__out(ex_mem_1_memread__out), .MemWrite__in(id_ex_1_p20),
    .MemWrite__out(ex_mem_1_memwrite__out), .RegWrite__in(id_ex_1_p18),
    .RegWrite__out(ex_mem_1_regwrite__out), .RegDest__in(multiplexer_7_out),
    .RegDest__out(ex_mem_1_regdest__out));  // open: PC__in, Zero__in, PC__out, Zero__out
  Bit_Extender #(.in_width(32), .out_width(24)) bit_extender_3 (.in(Result_2), .out(bit_extender_3_out));
  // MIPS_RAM mips_ram_1: pin names not known; wires that end beside it: bit_extender_3_out, ex_mem_1_inst___out, ex_mem_1_memwrite__out, ex_mem_1_memread__out, Tick, Data
  MEM_WB mem_wb_1 (
    .Clock(Tick), .Read_Data__in(Data), .Address__in(Result_2), .Read_Data__out(mem_wb_1_read_data__out),
    .Address__out(mem_wb_1_address__out), .MemToReg__in(ex_mem_1_memtoreg__out),
    .MemToReg__out(mem_wb_1_memtoreg__out), .RegWrite__in(ex_mem_1_regwrite__out),
    .RegWrite__out(registerfile_1_p3), .RegDest__in(ex_mem_1_regdest__out), .RegDest__out(registerfile_1_p4));
  not not_4 (not_4_out, mem_wb_1_memtoreg__out);
  Multiplexer #(.width(32), .enable("false")) multiplexer_12 (
    .in0(mem_wb_1_read_data__out), .in1(mem_wb_1_address__out), .out(Write_Back), .sel(not_4_out));

  assign B_3 = B_2;
  assign Operation_Code = Fetched_Instruction[31:26];
  assign Operation_Code_2 = Fetched_Instruction[25:21];
endmodule

module ALU_control (
  input  [7:0] in_1,
  output [3:0] out_2
);

  // PLA pla_1: pin names not known; wires that end beside it: in_1, out_2
endmodule

module Imm__Ctrl (
  input  [2:0] in_1,
  output [3:0] out_2
);

  // PLA Imm__Ctrl: pin names not known; wires that end beside it: in_1, out_2
endmodule

module IF_ID (
  input  Clock,
  input  [31:0] PC__in,
  input  [31:0] Inst___in,
  output [31:0] PC__out,
  output [31:0] Inst___out
);

  Register #(.width(32)) register_1 (.D(PC__in), .Q(PC__out), .clk(Clock));  // open: en, clr
  Register #(.width(32)) register_2 (.D(Inst___in), .Q(Inst___out), .clk(Clock));  // open: en, clr

  // Other names for the same wires on the sheet: Tick = Clock
endmodule

module ID_EX (
  input  Clock,
  input  [31:0] PC__in,
  input  [31:0] A__in,
  input  [31:0] B__in,
  input  [31:0] Inst___in,
  input  [5:0] opcode__in,
  input  [4:0] _20_16__I_dest___in,
  input  [4:0] _15_11__R_dest___in,
  input  MemToReg__in,
  input  RegDst__in,
  input  RegWrite__in,
  input  MemRead__in,
  input  MemWrite__in,
  input  ALUSrc__in,
  input  Branch__in,
  input  [1:0] ALUOp__in,
  input  Jump__in,
  input  JumpReg__in,
  output [31:0] PC__out,
  output [31:0] A__out,
  output [31:0] B__out,
  output [31:0] inst___out,
  output [5:0] opcode__out,
  output [4:0] _20_16__I_dest___out,
  output [4:0] _15_11__R_dest___out,
  output MemToReg__out,
  output RegDst__out,
  output RegWrite__out,
  output MemRead__out,
  output MemWrite__out,
  output ALUSrc__out,
  output Branch__out,
  output [1:0] ALUOp__out,
  output Jump__out,
  output JumpReg__out
);

  Register #(.width(32)) register_1 (.D(PC__in), .Q(PC__out), .clk(Clock));  // open: en, clr
  Register #(.width(32)) register_2 (.D(A__in), .Q(A__out), .clk(Clock));  // open: en, clr
  Register #(.width(32)) register_3 (.D(B__in), .Q(B__out), .clk(Clock));  // open: en, clr
  Register #(.width(32)) register_4 (.D(Inst___in), .Q(inst___out), .clk(Clock));  // open: en, clr
  Register #(.width(6)) register_5 (.D(opcode__in), .Q(opcode__out), .clk(Clock));  // open: en, clr
  Register #(.width(5)) register_6 (.D(_20_16__I_dest___in), .Q(_20_16__I_dest___out), .clk(Clock));  // open: en, clr
  Register #(.width(5)) register_7 (.D(_15_11__R_dest___in), .Q(_15_11__R_dest___out), .clk(Clock));  // open: en, clr
  Register #(.width(1)) register_8 (.D(MemToReg__in), .Q(MemToReg__out), .clk(Clock));  // open: en, clr
  Register #(.width(1)) register_9 (.D(RegDst__in), .Q(RegDst__out), .clk(Clock));  // open: en, clr
  Register #(.width(1)) register_10 (.D(RegWrite__in), .Q(RegWrite__out), .clk(Clock));  // open: en, clr
  Register #(.width(1)) register_11 (.D(MemRead__in), .Q(MemRead__out), .clk(Clock));  // open: en, clr
  Register #(.width(1)) register_12 (.D(MemWrite__in), .Q(MemWrite__out), .clk(Clock));  // open: en, clr
  Register #(.width(1)) register_13 (.D(ALUSrc__in), .Q(ALUSrc__out), .clk(Clock));  // open: en, clr
  Register #(.width(1)) register_14 (.D(Branch__in), .Q(Branch__out), .clk(Clock));  // open: en, clr
  Register #(.width(2)) register_15 (.D(ALUOp__in), .Q(ALUOp__out), .clk(Clock));  // open: en, clr
  Register #(.width(1)) register_16 (.D(Jump__in), .Q(Jump__out), .clk(Clock));  // open: en, clr
  Register #(.width(1)) register_17 (.D(JumpReg__in), .Q(JumpReg__out), .clk(Clock));  // open: en, clr

  // Other names for the same wires on the sheet: Tick = Clock

  // Notes on the sheet:
  //   WB
  //   M
  //   EX
endmodule

module EX_MEM (
  input  Clock,
  input  [31:0] PC__in,
  input  Zero__in,
  input  [31:0] Result__in,
  input  [31:0] Inst___in,
  input  [4:0] RegDest__in,
  input  MemToReg__in,
  input  RegWrite__in,
  input  MemRead__in,
  input  MemWrite__in,
  output [31:0] PC__out,
  output Zero__out,
  output [31:0] Result__out,
  output [31:0] inst___out,
  output [4:0] RegDest__out,
  output MemToReg__out,
  output RegWrite__out,
  output MemRead__out,
  output MemWrite__out
);

  Register #(.width(32)) register_1 (.D(PC__in), .Q(PC__out), .clk(Clock));  // open: en, clr
  Register #(.width(1)) register_2 (.D(Zero__in), .Q(Zero__out), .clk(Clock));  // open: en, clr
  Register #(.width(32)) register_3 (.D(Result__in), .Q(Result__out), .clk(Clock));  // open: en, clr
  Register #(.width(32)) register_4 (.D(Inst___in), .Q(inst___out), .clk(Clock));  // open: en, clr
  Register #(.width(5)) register_5 (.D(RegDest__in), .Q(RegDest__out), .clk(Clock));  // open: en, clr
  Register #(.width(1)) register_6 (.D(MemToReg__in), .Q(MemToReg__out), .clk(Clock));  // open: en, clr
  Register #(.width(1)) register_7 (.D(RegWrite__in), .Q(RegWrite__out), .clk(Clock));  // open: en, clr
  Register #(.width(1)) register_8 (.D(MemRead__in), .Q(MemRead__out), .clk(Clock));  // open: en, clr
  Register #(.width(1)) register_9 (.D(MemWrite__in), .Q(MemWrite__out), .clk(Clock));  // open: en, clr

  // Other names for the same wires on the sheet: Tick = Clock

  // Notes on the sheet:
  //   WB
  //   M
endmodule

module MEM_WB (
  input  Clock,
  input  [31:0] Read_Data__in,
  input  [31:0] Address__in,
  input  [4:0] RegDest__in,
  input  MemToReg__in,
  input  RegWrite__in,
  output [31:0] Read_Data__out,
  output [31:0] Address__out,
  output [4:0] RegDest__out,
  output MemToReg__out,
  output RegWrite__out
);

  Register #(.width(32)) register_1 (.D(Read_Data__in), .Q(Read_Data__out), .clk(Clock));  // open: en, clr
  Register #(.width(32)) register_2 (.D(Address__in), .Q(Address__out), .clk(Clock));  // open: en, clr
  Register #(.width(5)) register_3 (.D(RegDest__in), .Q(RegDest__out), .clk(Clock));  // open: en, clr
  Register #(.width(1)) register_4 (.D(MemToReg__in), .Q(MemToReg__out), .clk(Clock));  // open: en, clr
  Register #(.width(1)) register_5 (.D(RegWrite__in), .Q(RegWrite__out), .clk(Clock));  // open: en, clr

  // Other names for the same wires on the sheet: Tick = Clock

  // Notes on the sheet:
  //   WB
endmodule
