// Logisim project sandbox_forward.circ as structural Verilog: 8 circuits, main circuit main
module main (
  output [31:0] Jump_Address,
  output [31:0] Fetched_Instruction,
  output [31:0] A,
  output [31:0] A_2,
  output [31:0] B,
  output [31:0] B_2,
  output [31:0] Result,
  output [31:0] Next_Instruction,
  output [31:0] Data,
  output [5:0] Operation_Code,
  output [31:0] B_3,
  output [31:0] Result_2,
  output [31:0] _0_15,
  output [3:0] out_14,
  output [31:0] _0_15_2,
  output [31:0] Write_Back,
  output [15:0] out_17,
  output [2:0] out_18,
  output [1:0] out_19,
  output [1:0] out_20
);

  wire ALUSrc, and_1_out, Branch, comparator_2_eq, ex_mem_1_memread__out, ex_mem_1_memtoreg__out,
       ex_mem_1_memwrite__out, ex_mem_1_regwrite__out, id_ex_1_alusrc__out, id_ex_1_memread__out,
       id_ex_1_memtoreg__out, id_ex_1_memwrite__out, id_ex_1_regwrite__out, JAL, JumpReg,
       mem_wb_1_memtoreg__out, mem_wb_1_regwrite__out, MemRead, MemToReg, MemWrite, nor_1_out, not_1_out,
       not_2_out, or_1_out, RegDst, RegWrite, Tick;
  wire [1:0] ALUOp, id_ex_1_aluop__out;
  wire [3:0] alu_control_1_out_2, mips_alu_1_p3;
  wire [4:0] ex_mem_1_regdest__out, id_ex_1_regdest__out, id_ex_1_rs__out, id_ex_1_rt__out,
       mem_wb_1_regdest__out, multiplexer_5_out, multiplexer_6_out, multiplexer_8_out;
  wire [5:3] id_ex_1_opcode__out;
  wire [23:0] bit_extender_3_out;
  wire [27:0] bit_extender_1_out, if_id_1_pc__out;
  wire [31:0] adder_1_p3, adder_2_p4, adder_3_p3, ex_mem_1_inst___out, if_id_1_return_adress__out,
       mem_wb_1_address__out, mem_wb_1_read_data__out, multiplexer_1_out, multiplexer_2_out,
       multiplexer_3_out, multiplexer_4_out, multiplexer_7_out, multiplexer_9_out, multiplexer_10_out,
       multiplexer_11_out, PC_q, shifter_2_out;

  Multiplexer #(.width(32), .enable("false")) multiplexer_1 (
    .in0(multiplexer_2_out), .in1(adder_1_p3), .out(multiplexer_1_out), .sel(nor_1_out));
  nor nor_1 (nor_1_out, JAL, JumpReg, and_1_out);
  Register #(.width(32)) PC (.D(multiplexer_1_out), .Q(PC_q), .clk(Tick));  // open: en, clr
  // Adder adder_1: pin names not known; wires that end beside it: PC_q, 32'h4, adder_1_p3
  // Adder adder_2: pin names not known; wires that end beside it: PC_q, 32'h8, PC_q, adder_2_p4
  Clock clock_1 (.out(Tick));
  // MIPSProgramROM mipsprogramrom_1: pin names not known; wires that end beside it: Next_Instruction
  IF_ID if_id_1 (
    .Clock(Tick), .PC__in(adder_1_p3), .Inst___in(Next_Instruction),
    .PC__out({Jump_Address[31:28], if_id_1_pc__out}), .Inst___out(Fetched_Instruction),
    .Return_Adress__in(adder_2_p4), .Return_Adress__out(if_id_1_return_adress__out));
  // PLA Control: pin names not known; wires that end beside it: Fetched_Instruction[31:26]
  Multiplexer #(.width(32), .enable("false")) multiplexer_2 (
    .in0(multiplexer_4_out), .in1(A_2), .out(multiplexer_2_out), .sel(JumpReg));
  Comparator comparator_1 (.a({ALUOp, _0_15[5:0]}), .b(8'h88), .eq(JumpReg));  // open: gt, lt
  assign bit_extender_1_out = {{2{1'b0}}, Fetched_Instruction[25:0]};  // Bit_Extender bit_extender_1
  Multiplexer #(.width(32), .enable("false")) multiplexer_3 (
    .in0(if_id_1_return_adress__out), .in1(Write_Back), .out(multiplexer_3_out), .sel(not_1_out));
  Multiplexer #(.width(32), .enable("false")) multiplexer_4 (
    .in0(multiplexer_7_out), .in1(Jump_Address), .out(multiplexer_4_out), .sel(JAL));
  not not_1 (not_1_out, JAL);
  Shifter #(.width(28)) shifter_1 (.in(bit_extender_1_out), .\dist (5'b00010), .out(Jump_Address[27:0]));
  or or_1 (or_1_out, mem_wb_1_regwrite__out, JAL);
  Multiplexer #(.width(5), .enable("false")) multiplexer_5 (
    .in0(mem_wb_1_regdest__out), .in1(multiplexer_8_out), .out(multiplexer_5_out), .sel(JAL));
  // RegisterFile registerfile_1: pin names not known; wires that end beside it: multiplexer_3_out, Tick, or_1_out, multiplexer_5_out, Fetched_Instruction[25:21], Fetched_Instruction[20:16], A_2, B
  assign _0_15 = {{16{Fetched_Instruction[15]}}, Fetched_Instruction[15:0]};  // Bit_Extender bit_extender_2
  and and_1 (and_1_out, Branch, comparator_2_eq);
  Comparator #(.width(32), .mode("unsigned")) comparator_2 (.a(A_2), .b(B), .eq(comparator_2_eq));  // open: gt, lt
  Shifter #(.width(32)) shifter_2 (.in(_0_15), .\dist (5'b00010), .out(shifter_2_out));
  Multiplexer #(.width(5), .enable("false")) multiplexer_6 (
    .in0(Fetched_Instruction[20:16]), .in1(Fetched_Instruction[15:11]), .out(multiplexer_6_out), .sel(RegDst));
  Multiplexer #(.width(32), .enable("false")) multiplexer_7 (
    .in0({Jump_Address[31:28], if_id_1_pc__out}), .in1(adder_3_p3), .out(multiplexer_7_out), .sel(and_1_out));
  // Adder adder_3: pin names not known; wires that end beside it: {Jump_Address[31:28], if_id_1_pc__out}, shifter_2_out, adder_3_p3
  Multiplexer #(.width(5), .enable("false")) multiplexer_8 (
    .in0(multiplexer_6_out), .in1({5{1'b1}}), .out(multiplexer_8_out), .sel(JAL));
  ID_EX id_ex_1 (
    .Clock(Tick), .PC__in({Jump_Address[31:28], if_id_1_pc__out}), .A__in(A_2), .B__in(B), .Inst___in(_0_15),
    .A__out(A), .B__out(B_2), .inst___out(_0_15_2), .MemToReg__in(MemToReg),
    .MemToReg__out(id_ex_1_memtoreg__out), .MemRead__in(MemRead), .MemRead__out(id_ex_1_memread__out),
    .MemWrite__in(MemWrite), .MemWrite__out(id_ex_1_memwrite__out), .ALUSrc__in(ALUSrc),
    .ALUSrc__out(id_ex_1_alusrc__out), .ALUOp__in(ALUOp), .ALUOp__out(id_ex_1_aluop__out),
    .RegWrite__in(RegWrite), .RegWrite__out(id_ex_1_regwrite__out), .regdest__in(multiplexer_8_out),
    .regdest__out(id_ex_1_regdest__out), .opcode__in(Fetched_Instruction[31:26]),
    .opcode__out({id_ex_1_opcode__out, out_18}), .rs__in(Fetched_Instruction[25:21]),
    .rs__out(id_ex_1_rs__out), .rt__in(Fetched_Instruction[20:16]), .rt__out(id_ex_1_rt__out));  // open: PC__out, RegDst__in, RegDst__out, Branch__in, Branch__out, Jump__in, Jump__out, JumpReg__in, JumpReg__out
  Multiplexer #(.select(2), .width(32), .enable("false")) multiplexer_9 (
    .in0(A), .in1(Write_Back), .in2(Result_2), .out(multiplexer_9_out), .sel(out_20));  // open: in3
  Multiplexer #(.width(32), .enable("false")) multiplexer_10 (
    .in0(multiplexer_11_out), .in1(_0_15_2), .out(multiplexer_10_out), .sel(id_ex_1_alusrc__out));
  Multiplexer #(.select(2), .width(32), .enable("false")) multiplexer_11 (
    .in0(B_2), .in1(Write_Back), .in2(Result_2), .out(multiplexer_11_out), .sel(out_19));  // open: in3
  ALU_control alu_control_1 (.in_1({id_ex_1_aluop__out, _0_15_2[5:0]}), .out_2(alu_control_1_out_2));
  Forwarding_unit forwarding_unit_1 (
    .A__out(out_20), .B__out(out_19), .rs__in(id_ex_1_rs__out), .rt__in(id_ex_1_rt__out),
    .MEM_WB_RegisterRd(mem_wb_1_regdest__out), .EX_MEM_RegisterRd(ex_mem_1_regdest__out),
    .EX_MEM_RegWrite__in(ex_mem_1_regwrite__out), .MEM_WB_RegWrite__in(mem_wb_1_regwrite__out));
  // MIPS_ALU mips_alu_1: pin names not known; wires that end beside it: multiplexer_9_out, multiplexer_10_out, mips_alu_1_p3, Result
  Multiplexer #(.width(4), .enable("false")) multiplexer_12 (
    .in0(alu_control_1_out_2), .in1(out_14), .out(mips_alu_1_p3), .sel(alu_control_1_out_2[3]));
  Imm__Ctrl imm_ctrl_1 (.in_1(out_18), .out_2(out_14));
  EX_MEM ex_mem_1 (
    .Clock(Tick), .Result__in(Result), .Inst___in(B_2), .Result__out(Result_2),
    .inst___out(ex_mem_1_inst___out), .MemToReg__in(id_ex_1_memtoreg__out),
    .MemToReg__out(ex_mem_1_memtoreg__out), .MemRead__in(id_ex_1_memread__out),
    .MemRead__out(ex_mem_1_memread__out), .MemWrite__in(id_ex_1_memwrite__out),
    .MemWrite__out(ex_mem_1_memwrite__out), .RegWrite__in(id_ex_1_regwrite__out),
    .RegWrite__out(ex_mem_1_regwrite__out), .RegDest__in(id_ex_1_regdest__out),
    .RegDest__out(ex_mem_1_regdest__out));  // open: PC__in, Zero__in, PC__out, Zero__out
  Bit_Extender #(.in_width(32), .out_width(24)) bit_extender_3 (.in(Result_2), .out(bit_extender_3_out));
  // MIPS_RAM mips_ram_1: pin names not known; wires that end beside it: bit_extender_3_out, ex_mem_1_inst___out, ex_mem_1_memwrite__out, ex_mem_1_memread__out, Tick, Data
  MEM_WB mem_wb_1 (
    .Clock(Tick), .Read_Data__in(Data), .Address__in(Result_2), .Read_Data__out(mem_wb_1_read_data__out),
    .Address__out(mem_wb_1_address__out), .MemToReg__in(ex_mem_1_memtoreg__out),
    .MemToReg__out(mem_wb_1_memtoreg__out), .RegWrite__in(ex_mem_1_regwrite__out),
    .RegWrite__out(mem_wb_1_regwrite__out), .RegDest__in(ex_mem_1_regdest__out),
    .RegDest__out(mem_wb_1_regdest__out));
  not not_2 (not_2_out, mem_wb_1_memtoreg__out);
  Multiplexer #(.width(32), .enable("false")) multiplexer_13 (
    .in0(mem_wb_1_read_data__out), .in1(mem_wb_1_address__out), .out(Write_Back), .sel(not_2_out));

  assign B_3 = B_2;
  assign Operation_Code = Fetched_Instruction[31:26];
  assign out_17 = Fetched_Instruction[15:0];
endmodule

module ALU_control (
  input  [7:0] in_1,
  output [3:0] out_2
);

  // PLA pla_1: pin names not known; wires that end beside it: in_1, out_2
endmodule

module Imm__Ctrl (
  input  [2:0] in_1,
  output [3:0] out_2
);

  // PLA Imm__Ctrl: pin names not known; wires that end beside it: in_1, out_2
endmodule

module IF_ID (
  input  Clock,
  input  [31:0] PC__in,
  input  [31:0] Inst___in,
  input  [31:0] Return_Adress__in,
  output [31:0] PC__out,
  output [31:0] Inst___out,
  output [31:0] Return_Adress__out
);

  Register #(.width(32)) register_1 (.D(PC__in), .Q(PC__out), .clk(Clock));  // open: en, clr
  Register #(.width(32)) register_2 (.D(Inst___in), .Q(Inst___out), .clk(Clock));  // open: en, clr
  Register #(.width(32)) register_3 (.D(Return_Adress__in), .Q(Return_Adress__out), .clk(Clock));  // open: en, clr

  // Other names for the same wires on the sheet: Tick = Clock
endmodule

module ID_EX (
  input  Clock,
  input  [31:0] PC__in,
  input  [31:0] A__in,
  input  [31:0] B__in,
  input  [31:0] Inst___in,
  input  [5:0] opcode__in,
  input  [4:0] regdest__in,
  input  [4:0] rs__in,
  input  [4:0] rt__in,
  input  MemToReg__in,
  input  RegDst__in,
  input  RegWrite__in,
  input  MemRead__in,
  input  MemWrite__in,
  input  ALUSrc__in,
  input  Branch__in,
  input  [1:0] ALUOp__in,
  input  Jump__in,
  input  JumpReg__in,
  output [31:0] PC__out,
  output [31:0] A__out,
  output [31:0] B__out,
  output [31:0] inst___out,
  output [5:0] opcode__out,
  output [4:0] regdest__out,
  output [4:0] rs__out,
  output [4:0] rt__out,
  output MemToReg__out,
  output RegDst__out,
  output RegWrite__out,
  output MemRead__out,
  output MemWrite__out,
  output ALUSrc__out,
  output Branch__out,
  output [1:0] ALUOp__out,
  output Jump__out,
  output JumpReg__out
);

  Register #(.width(32)) register_1 (.D(PC__in), .Q(PC__out), .clk(Clock));  // open: en, clr
  Register #(.width(32)) register_2 (.D(A__in), .Q(A__out), .clk(Clock));  // open: en, clr
  Register #(.width(32)) register_3 (.D(B__in), .Q(B__out), .clk(Clock));  // open: en, clr
  Register #(.width(32)) register_4 (.D(Inst___in), .Q(inst___out), .clk(Clock));  // open: en, clr
  Register #(.width(6)) register_5 (.D(opcode__in), .Q(opcode__out), .clk(Clock));  // open: en, clr
  Register #(.width(5)) register_6 (.D(regdest__in), .Q(regdest__out), .clk(Clock));  // open: en, clr
  Register #(.width(5)) register_7 (.D(rs__in), .Q(rs__out), .clk(Clock));  // open: en, clr
  Register #(.width(5)) register_8 (.D(rt__in), .Q(rt__out), .clk(Clock));  // open: en, clr
  Register #(.width(1)) register_9 (.D(MemToReg__in), .Q(MemToReg__out), .clk(Clock));  // open: en, clr
  Register #(.width(1)) register_10 (.D(RegDst__in), .Q(RegDst__out), .clk(Clock));  // open: en, clr
  Register #(.width(1)) register_11 (.D(RegWrite__in), .Q(RegWrite__out), .clk(Clock));  // open: en, clr
  Register #(.width(1)) register_12 (.D(MemRead__in), .Q(MemRead__out), .clk(Clock));  // open: en, clr
  Register #(.width(1)) register_13 (.D(MemWrite__in), .Q(MemWrite__out), .clk(Clock));  // open: en, clr
  Register #(.width(1)) register_14 (.D(ALUSrc__in), .Q(ALUSrc__out), .clk(Clock));  // open: en, clr
  Register #(.width(1)) register_15 (.D(Branch__in), .Q(Branch__out), .clk(Clock));  // open: en, clr
  Register #(.width(2)) register_16 (.D(ALUOp__in), .Q(ALUOp__out), .clk(Clock));  // open: en, clr
  Register #(.width(1)) register_17 (.D(Jump__in), .Q(Jump__out), .clk(Clock));  // open: en, clr
  Register #(.width(1)) register_18 (.D(JumpReg__in), .Q(JumpReg__out), .clk(Clock));  // open: en, clr

  // Other names for the same wires on the sheet: Tick = Clock

  // Notes on the sheet:
  //   WB
  //   M
  //   EX
endmodule

module EX_MEM (
  input  Clock,
  input  [31:0] PC__in,
  input  Zero__in,
  input  [31:0] Result__in,
  input  [31:0] Inst___in,
  input  [4:0] RegDest__in,
  input  MemToReg__in,
  input  RegWrite__in,
  input  MemRead__in,
  input  MemWrite__in,
  output [31:0] PC__out,
  output Zero__out,
  output [31:0] Result__out,
  output [31:0] inst___out,
  output [4:0] RegDest__out,
  output MemToReg__out,
  output RegWrite__out,
  output MemRead__out,
  output MemWrite__out
);

  Register #(.width(32)) register_1 (.D(PC__in), .Q(PC__out), .clk(Clock));  // open: en, clr
  Register #(.width(1)) register_2 (.D(Zero__in), .Q(Zero__out), .clk(Clock));  // open: en, clr
  Register #(.width(32)) register_3 (.D(Result__in), .Q(Result__out), .clk(Clock));  // open: en, clr
  Register #(.width(32)) register_4 (.D(Inst___in), .Q(inst___out), .clk(Clock));  // open: en, clr
  Register #(.width(5)) register_5 (.D(RegDest__in), .Q(RegDest__out), .clk(Clock));  // open: en, clr
  Register #(.width(1)) register_6 (.D(MemToReg__in), .Q(MemToReg__out), .clk(Clock));  // open: en, clr
  Register #(.width(1)) register_7 (.D(RegWrite__in), .Q(RegWrite__out), .clk(Clock));  // open: en, clr
  Register #(.width(1)) register_8 (.D(MemRead__in), .Q(MemRead__out), .clk(Clock));  // open: en, clr
  Register #(.width(1)) register_9 (.D(MemWrite__in), .Q(MemWrite__out), .clk(Clock));  // open: en, clr

  // Other names for the same wires on the sheet: Tick = Clock

  // Notes on the sheet:
  //   WB
  //   M
endmodule

module MEM_WB (
  input  Clock,
  input  [31:0] Read_Data__in,
  input  [31:0] Address__in,
  input  [4:0] RegDest__in,
  input  MemToReg__in,
  input  RegWrite__in,
  output [31:0] Read_Data__out,
  output [31:0] Address__out,
  output [4:0] RegDest__out,
  output MemToReg__out,
  output RegWrite__out
);

  Register #(.width(32)) register_1 (.D(Read_Data__in), .Q(Read_Data__out), .clk(Clock));  // open: en, clr
  Register #(.width(32)) register_2 (.D(Address__in), .Q(Address__out), .clk(Clock));  // open: en, clr
  Register #(.width(5)) register_3 (.D(RegDest__in), .Q(RegDest__out), .clk(Clock));  // open: en, clr
  Register #(.width(1)) register_4 (.D(MemToReg__in), .Q(MemToReg__out), .clk(Clock));  // open: en, clr
  Register #(.width(1)) register_5 (.D(RegWrite__in), .Q(RegWrite__out), .clk(Clock));  // open: en, clr

  // Other names for the same wires on the sheet: Tick = Clock

  // Notes on the sheet:
  //   WB
endmodule

module Forwarding_unit (
  input  [4:0] rs__in,
  input  EX_MEM_RegWrite__in,
  input  [4:0] EX_MEM_RegisterRd,
  input  [4:0] rt__in,
  input  MEM_WB_RegWrite__in,
  input  [4:0] MEM_WB_RegisterRd,
  output [1:0] A__out,
  output [1:0] B__out
);

  wire and_1_out, and_2_out, comparator_1_eq, comparator_2_eq, comparator_3_eq, comparator_4_eq,
       comparator_5_eq, comparator_6_eq, nand_1_out, nand_2_out;

  Comparator #(.width(5)) comparator_1 (.a(EX_MEM_RegisterRd), .b(rs__in), .eq(comparator_1_eq));  // open: gt, lt
  Comparator #(.width(5)) comparator_2 (.a(rt__in), .b(EX_MEM_RegisterRd), .eq(comparator_2_eq));  // open: gt, lt
  Comparator #(.width(5)) comparator_3 (.a(MEM_WB_RegisterRd), .b(rs__in), .eq(comparator_3_eq));  // open: gt, lt
  Comparator #(.width(5)) comparator_4 (.a(rt__in), .b(MEM_WB_RegisterRd), .eq(comparator_4_eq));  // open: gt, lt
  Comparator #(.width(5)) comparator_5 (.a(EX_MEM_RegisterRd), .b({5{1'b0}}), .eq(comparator_5_eq));  // open: gt, lt
  Comparator #(.width(5)) comparator_6 (.a(MEM_WB_RegisterRd), .b({5{1'b0}}), .eq(comparator_6_eq));  // open: gt, lt
  and and_1 (and_1_out, EX_MEM_RegWrite__in, ~comparator_5_eq);  // AND_Gate
  and and_2 (and_2_out, MEM_WB_RegWrite__in, ~comparator_6_eq);  // AND_Gate
  nand nand_1 (nand_1_out, ~comparator_1_eq, and_1_out);  // NAND_Gate
  nand nand_2 (nand_2_out, and_1_out, ~comparator_2_eq);  // NAND_Gate
  and and_3 (A__out[1], comparator_1_eq, and_1_out);
  and and_4 (B__out[1], and_1_out, comparator_2_eq);
  and and_5 (A__out[0], comparator_3_eq, nand_1_out, and_2_out);
  and and_6 (B__out[0], and_2_out, nand_2_out, comparator_4_eq);

  // Notes on the sheet:
  //   EX/MEM.RegisterRd == ID/EX.RegisterRs
  //   EX/MEM.RegisterRd == ID/EX.RegisterRt
  //   MEM/WB.RegisterRd == ID/EX.RegisterRs
  //   MEM/WB.RegisterRd == ID/EX.RegisterRt
  //   EX/MEM.ReqWrite && (EX/MEM.RegisterRd != 0x00)
  //   MEM/WB.ReqWrite && (MEM/WB.RegisterRd != 0x00)
endmodule
